# Fritzing sketch circuit (saved by Fritzing 0.9.3b)
breadboards: 1

parts:
  Launchpad1 = TI Launchpad MSP430G2
  LED1 = smd LED [color="Red (633nm)" package="0603 [SMD]"]
  R1 = Resistor [tolerance=±5% resistance=100 package="0603 [SMD]"]
  LED2 = smd LED [color="Red (633nm)" package="0603 [SMD]"]
  R2 = Resistor [tolerance=±5% resistance=100 package="0603 [SMD]"]
  LED3 = smd LED [color="Red (633nm)" package="0603 [SMD]"]
  R3 = Resistor [tolerance=±5% resistance=100 package="0603 [SMD]"]
  LED4 = smd LED [color="Red (633nm)" package="0603 [SMD]"]
  R4 = Resistor [tolerance=±5% resistance=100 package="0603 [SMD]"]
  LED5 = smd LED [color="Red (633nm)" package="0603 [SMD]"]
  LED6 = smd LED [color="Red (633nm)" package="0603 [SMD]"]
  LED7 = smd LED [color="Red (633nm)" package="0603 [SMD]"]
  LED8 = smd LED [color="Red (633nm)" package="0603 [SMD]"]
  R5 = Resistor [tolerance=±5% resistance=100 package="0603 [SMD]"]
  R6 = Resistor [tolerance=±5% resistance=100 package="0603 [SMD]"]
  R7 = Resistor [tolerance=±5% resistance=100 package="0603 [SMD]"]
  R8 = Resistor [tolerance=±5% resistance=100 package="0603 [SMD]"]

nets:
  N1: Launchpad1.p10, R8.Pin_0
  N2: Launchpad1.p9, R7.Pin_0
  N3: Launchpad1.p8, R6.Pin_0
  N4: Launchpad1.p7, R4.Pin_0
  N5: Launchpad1.p6, R3.Pin_0
  N6: Launchpad1.p5, R2.Pin_0
  N7: Launchpad1.p2, R1.Pin_0
  N8: Launchpad1.p11, R5.Pin_0
  N9: Launchpad1.p20, LED1.anode, LED2.anode, LED3.anode, LED4.anode, LED5.anode, LED6.anode, LED7.anode, LED8.anode
  N10: LED1.cathode, R1.Pin_1
  N11: LED2.cathode, R2.Pin_1
  N12: LED3.cathode, R3.Pin_1
  N13: LED4.cathode, R4.Pin_1
  N14: LED5.cathode, R6.Pin_1
  N15: LED6.cathode, R7.Pin_1
  N16: LED7.cathode, R8.Pin_1
  N17: LED8.cathode, R5.Pin_1
